# Fritzing sketch Untitled Sketch 2 (saved by Fritzing 0.9.3b)
breadboards: 1

parts:
  LCD1 = LCD screen
  Componente1 = Arduino Ethernet Shield (Rev3)
  Componente2 = Arduino Mega 2560 (Rev3)
  S1 = Momentary Switch [part_number="Botoeira Abrir Interna" package=ksa_sealed_tac_switch]
  R1 = Resistor [tolerance=±5% resistance=100 package="2512 [SMD]"]
  R2 = Resistor [tolerance=±5% resistance=330 package="2512 [SMD]"]
  LED1 = LED - 5mm [color="Red (633nm)" package="5 mm [THT]"]
  R3 = Resistor [tolerance=±5% resistance=330 package="2512 [SMD]"]
  LED2 = LED - 5mm [color="Yellow (595nm)" package="5 mm [THT]"]
  LED3 = LED - 5mm [color="Green (570nm)" package="5 mm [THT]"]
  R4 = Resistor [tolerance=±5% resistance=330 package="2512 [SMD]"]
  J1 = Piezo Speaker
  R5 = Resistor [tolerance=±5% resistance=100 package="2512 [SMD]"]
  KEYPAD1 = Membrane_Matrix_Keypad
  Q1 = Basic FET N-Channel [package="TO220 [THT]"]
  R6 = Resistor [tolerance=±5% resistance=220 package=THT]
  Componente3 = RFID-RC522-v2
  KY-1 = Keyes Relay [package=THT]

nets:
  VSS: LCD1.VSS, LCD1.R/W, Componente1.GND, S1.1, LED1.cathode, LED2.cathode, LED3.cathode, J1.pin1, Q1.source
  VDD: LCD1.VDD, Componente1.5V, R1.Pin_1
  N1: LCD1.V0, Componente1.PWM_D6
  N2: LCD1.RS, Componente2.D31
  N3: LCD1.E, Componente2.D30
  N4: LCD1.DB4, Componente2.D32
  N5: LCD1.DB5, Componente2.D33
  N6: LCD1.DB6, Componente2.D34
  N7: LCD1.DB7, Componente2.D35
  N8: LCD1.LED+, R1.Pin_0
  N9: LCD1.LED-, Q1.drain
  N10: Componente1.D7, R5.Pin_1
  N11: Componente2.3V3, Componente3.3_3V
  N12: Componente2.5V, KY-1.power
  GND: Componente2.GND, Componente3.GND, KY-1.ground
  N13: Componente2.D5_PWM, Componente3.RST
  N14: Componente2.D22, R2.Pin_1
  N15: Componente2.D24, R3.Pin_1
  N16: Componente2.D25, R6.Pin_1
  N17: Componente2.D26, R4.Pin_1
  N18: Componente2.D28, S1.3
  N19: Componente2.D36, KY-1.signal
  N20: Componente2.D38, KEYPAD1.connector7
  N21: Componente2.D39, KEYPAD1.connector6
  N22: Componente2.D40, KEYPAD1.connector5
  N23: Componente2.D42, KEYPAD1.connector4
  N24: Componente2.D43, KEYPAD1.connector3
  N25: Componente2.D44, KEYPAD1.connector2
  N26: Componente2.D45, KEYPAD1.connector1
  N27: Componente2.D50, Componente3.MISO
  N28: Componente2.D51, Componente3.MOSI
  N29: Componente2.D52, Componente3.SCK
  N30: Componente2.D53, Componente3.SDA
  N31: R2.Pin_0, LED1.anode
  N32: R3.Pin_0, LED2.anode
  N33: LED3.anode, R4.Pin_0
  N34: J1.pin2, R5.Pin_0
  N35: Q1.gate, R6.Pin_0

notes:
  Botoeira Interna (Abrir) S1
  Relê Porta
  Leitor RFID
  Alimentação 3.3v(Atenção)
  Buzzer
  FET Regula o Backlight do LCD
  Pode ser ligado direto ao PINO 25, (Observar corrente não passar de 20mA , regular com resistor +- 330 Ohms)

custom parts:
  RFID-RC522-v2: A simple China made RFID-RC522 Reader; do check the pin labels, as this is a MFRC522 based clone.
  Keyes Relay: The Keyes 5V relay module is suitable for SCM development, home appliance control. It uses a 5V~12V TIL control signal which can control DC / AC signal.
